# Fritzing sketch Fridgeye (saved by Fritzing 0.9.3b)
breadboards: 1

parts:
  Part1 = Photon
  R2 = Resistor [tolerance=±5% resistance=330 package=THT]
  Photocell = Photocell (LDR) [package=THT]
  T1 = TMP36 Temperature Sensor [package="TO92 [THT]"]

nets:
  N1: Part1.A0, R2.Pin_0, Photocell.pin_0
  N2: Part1.A4, T1.Vout
  GND: Part1.GND, R2.Pin_1, T1.GND
  N3: Part1.3V3, Photocell.pin_1, T1.+Vs

notes:
  +
  -
